# Fritzing sketch Balancing Cube (saved by Fritzing 1.0.3b)
circuit board: 7.3cm x 5.3cm

parts:
  ESP32 = LuaNode32 / ESP32 [part_number=ESP32S-PIN30]
  Motor_3 = male pin header, 8 pins [form="♂ (male)"]
  Motor_2 = male pin header, 8 pins [form="♂ (male)"]
  Motor_1 = male pin header, 8 pins [form="♂ (male)"]
  MPU6050 = male pin header, 4 pins [form="♂ (male)"]
  7805 = Voltage Regulator [package=to220-igo]
  C1 = Electrolytic Capacitor [capacitance=0.1mF voltage=35V package="100 mil [THT, electrolytic]"]
  R1 = Resistor [tolerance=±5% power=0.25W resistance=33k package=THT]
  R2 = Resistor [tolerance=±5% power=0.25W resistance=10k package=THT]
  C2 = Ceramic Capacitor [capacitance=100nF voltage=35V package="100 mil [THT, multilayer]"]
  WS2812B = male pin header, 3 pins [form="♂ (male)"]
  C3 = Ceramic Capacitor [capacitance=100nF voltage=35V package="100 mil [THT, multilayer]"]
  - = Pad [width=5 height=5 connect=center]
  + = Pad [width=5 height=5 connect=center]
  Pad3 = Pad [width=5 height=5 connect=center]
  Pad2 = Pad [width=5 height=5 connect=center]
  S2 = male pin header, 3 pins [form="♂ (male)"]
  S3 = male pin header, 3 pins [form="♂ (male)"]
  S1 = male pin header, 3 pins [form="♂ (male)"]
  Buzz = Piezo Speaker

nets:
  N1: ESP32.D34, R1.Pin_0, R2.Pin_1, C2.1
  N2: ESP32.D35, Motor_1.pin1
  N3: ESP32.D32, Motor_1.pin5
  N4: ESP32.D33, Motor_1.pin2
  N5: ESP32.D25, Motor_2.pin5
  N6: ESP32.D26, Motor_3.pin6, Motor_2.pin6, Motor_1.pin6
  N7: ESP32.D27, Buzz.pin1
  N8: ESP32.D14, Motor_2.pin2
  N9: ESP32.D12, S2.pin1
  N10: ESP32.D13, Motor_2.pin1
  GND: ESP32.GND, Motor_3.pin7, Motor_2.pin7, Motor_1.pin7, MPU6050.pin2, 7805.GND, C1.-, R2.Pin_0, C2.0, WS2812B.pin2, C3.1, -.pad, Pad3.pad, S2.pin3, S3.pin3, S1.pin3, Buzz.pin2
  N11: ESP32.Vin, MPU6050.pin1, 7805.OUT, C1.+, WS2812B.pin1, C3.0, S2.pin2, S3.pin2, S1.pin2
  N12: ESP32.3V3, Motor_3.pin3, Motor_2.pin3, Motor_1.pin3
  N13: ESP32.D15, Motor_2.pin4
  N14: ESP32.D2, S1.pin1
  N15: ESP32.D4, Motor_1.pin4
  N16: ESP32.RX2, Motor_3.pin1
  N17: ESP32.TX2, Motor_3.pin2
  N18: ESP32.D5, Motor_3.pin4
  N19: ESP32.D18, Motor_3.pin5
  N20: ESP32.D19, WS2812B.pin3
  N21: ESP32.D21, MPU6050.pin4
  N22: ESP32.D22, MPU6050.pin3
  N23: ESP32.D23, S3.pin1
  N24: Motor_3.pin8, Motor_2.pin8, Motor_1.pin8, 7805.IN, R1.Pin_1, +.pad, Pad2.pad

notes:
  @richimoeller
  1
  8

custom parts:
  LuaNode32 / ESP32: New Image for LuaNode32 DOIT ESP32 DEVKIT V1. Base parts from LuaNode32 / ESP32 ESP32 based LuaNode32 by G.Noorlander DOIT Esp32 DevKit v1 (30 pins long, 11 pins width) by Werner Rothschopf (modified by vanepp Dec 2018)
